// Logisim project FINAL_expense_calci_formatted.circ as structural Verilog
module main (
  input  in_1
);

  wire and_1_out, and_2_out, and_3_out, and_4_out, and_5_out, and_6_out, and_7_out, and_8_out, and_9_out,
       and_10_out, and_11_out, and_12_out, and_13_out, and_14_out, and_15_out, and_16_out, and_17_out,
       and_18_out, and_19_out, bcd_adder_2_out_11, bcd_adder_3_out_11, bcd_adder_4_out_11,
       bcd_adder_5_out_12, bcd_adder_5_out_13, bcd_adder_5_out_14, bcd_adder_5_out_15, bcd_adder_6_out_11,
       bcd_adder_6_out_12, bcd_adder_6_out_13, bcd_adder_6_out_14, bcd_adder_6_out_15, bcd_adder_7_out_11,
       bcd_adder_7_out_12, bcd_adder_7_out_13, bcd_adder_7_out_14, bcd_adder_7_out_15, bcd_adder_8_out_11,
       bcd_adder_8_out_12, bcd_adder_8_out_13, bcd_adder_8_out_14, bcd_adder_8_out_15, bcd_compare_1_out_9,
       bcd_compare_2_out_9, button_1_out, button_2_out, button_3_out, button_4_out, button_5_out,
       category_1_a_2, category_1_b_2, category_1_c, category_1_d, category_1_e, category_1_f, category_1_g,
       counter_1_out_10, counter_1_out_11, Counter_2_out_8, Counter_2_out_9, Counter_2_out_10,
       Counter_2_out_11, n2bit_decoder_1_out_4, n2bit_decoder_1_out_5, n2bit_decoder_1_out_6,
       n2bit_decoder_1_out_7, n2bit_decoder_2_out_4, n2bit_decoder_2_out_5, n2bit_decoder_2_out_6,
       n2bit_decoder_2_out_7, nor_1_out, not_1_out, not_2_out, not_3_out, one_cell_1_out_6, one_cell_1_out_7,
       one_cell_1_out_8, one_cell_1_out_9, one_cell_1_out_10, one_cell_1_out_11, one_cell_1_out_12,
       one_cell_1_out_13, one_cell_1_out_14, one_cell_1_out_15, one_cell_1_out_16, one_cell_2_out_6,
       one_cell_2_out_7, one_cell_2_out_8, one_cell_2_out_9, one_cell_2_out_10, one_cell_2_out_15,
       one_cell_2_out_16, one_cell_3_out_6, one_cell_3_out_7, one_cell_3_out_8, one_cell_3_out_9,
       one_cell_3_out_10, one_cell_3_out_11, one_cell_3_out_12, one_cell_3_out_13, one_cell_3_out_14,
       one_cell_3_out_15, one_cell_3_out_16, one_cell_4_out_6, one_cell_4_out_7, one_cell_4_out_8,
       one_cell_4_out_9, one_cell_4_out_10, one_cell_4_out_15, one_cell_4_out_16, one_cell_5_out_6,
       one_cell_5_out_7, one_cell_5_out_8, one_cell_5_out_9, one_cell_5_out_10, one_cell_5_out_11,
       one_cell_5_out_12, one_cell_5_out_13, one_cell_5_out_14, one_cell_5_out_15, one_cell_5_out_16,
       one_cell_6_out_6, one_cell_6_out_7, one_cell_6_out_8, one_cell_6_out_9, one_cell_6_out_10,
       one_cell_6_out_15, one_cell_6_out_16, one_cell_7_out_6, one_cell_7_out_7, one_cell_7_out_8,
       one_cell_7_out_9, one_cell_7_out_10, one_cell_7_out_11, one_cell_7_out_12, one_cell_7_out_13,
       one_cell_7_out_14, one_cell_7_out_15, one_cell_7_out_16, one_cell_8_out_6, one_cell_8_out_7,
       one_cell_8_out_8, one_cell_8_out_9, one_cell_8_out_10, one_cell_8_out_15, one_cell_8_out_16, or_1_out,
       plus_1_out, sep_register_1_out_10, sep_register_1_out_11, sep_register_2_out_8, sep_register_2_out_9,
       sep_register_2_out_10, sep_register_2_out_11, sep_register_3_out_8, sep_register_3_out_9,
       sep_register_3_out_10, sep_register_3_out_11, sep_register_4_out_8, sep_register_4_out_9,
       sep_register_4_out_10, sep_register_4_out_11, sep_register_5_out_8, sep_register_5_out_9,
       sep_register_5_out_10, sep_register_5_out_11;
  wire [3:0] bcd_adder_1_out_15, bcd_adder_2_out_15, bcd_adder_3_out_15, bcd_adder_4_out_15,
       cumilative_expense_1_out_20, cumilative_expense_1_out_24, cumilative_expense_1_out_28,
       cumilative_expense_1_out_32, storage_4_bcd_1_out_20, storage_4_bcd_1_out_24, storage_4_bcd_1_out_28,
       storage_4_bcd_1_out_32, storage_4_bcd_2_out_20, storage_4_bcd_2_out_24, storage_4_bcd_2_out_28,
       storage_4_bcd_2_out_32;
  wire [15:0] cumilative_expense_2_out_20;

  LED led_1 ();  // open: in
  LED led_2 ();  // open: in
  LED led_3 (.in(bcd_compare_2_out_9));
  LED led_4 (.in(and_1_out));
  LED led_5 (.in(nor_1_out));
  Button plus_1 (.out(plus_1_out));
  Button button_1 (.out(button_1_out));
  Button button_2 (.out(button_2_out));
  Button button_3 (.out(button_3_out));
  Button button_4 (.out(button_4_out));
  Button button_5 (.out(button_5_out));
  LED led_6 ();  // open: in
  LED led_7 ();  // open: in
  not not_1 (not_1_out, bcd_compare_2_out_9);
  and and_1 (and_1_out, not_1_out, bcd_compare_1_out_9);
  bcd_adder bcd_adder_1 (
    .in_1(storage_4_bcd_1_out_32[3]), .in_2(storage_4_bcd_1_out_32[2]), .in_3(storage_4_bcd_1_out_32[1]),
    .in_4(storage_4_bcd_1_out_32[0]), .in_5(1'b0), .in_6(1'b0), .in_7(1'b0), .in_8(1'b0),
    .in_9(bcd_adder_2_out_11), .in_10(1'b1), .out_12(bcd_adder_1_out_15[3]), .out_13(bcd_adder_1_out_15[2]),
    .out_14(bcd_adder_1_out_15[1]), .out_15(bcd_adder_1_out_15[0]));  // open: out_11
  nor nor_1 (nor_1_out, bcd_compare_2_out_9, and_1_out);
  and and_2 (and_2_out, button_2_out, in_1);
  BCD_compare bcd_compare_1 (
    .in_1(bcd_adder_1_out_15), .in_2(storage_4_bcd_2_out_32), .in_3(bcd_adder_2_out_15),
    .in_4(storage_4_bcd_2_out_28), .in_5(bcd_adder_3_out_15), .in_6(storage_4_bcd_2_out_24),
    .in_7(bcd_adder_4_out_15), .in_8(storage_4_bcd_2_out_20), .out_9(bcd_compare_1_out_9));
  BCD_compare bcd_compare_2 (
    .in_1(storage_4_bcd_1_out_32), .in_2(storage_4_bcd_2_out_32), .in_3(storage_4_bcd_1_out_28),
    .in_4(storage_4_bcd_2_out_28), .in_5(storage_4_bcd_1_out_24), .in_6(storage_4_bcd_2_out_24),
    .in_7(storage_4_bcd_1_out_20), .in_8(storage_4_bcd_2_out_20), .out_9(bcd_compare_2_out_9));
  Counter counter_1 (
    .in_1(1'b0), .in_2(1'b0), .in_3(1'b1), .in_4(1'b1), .in_5(1'b1), .in_6(button_2_out),
    .in_7(button_3_out), .out_10(counter_1_out_10), .out_11(counter_1_out_11));  // open: out_8, out_9
  and and_3 (and_3_out, counter_1_out_10, in_1);
  and and_4 (and_4_out, counter_1_out_11, in_1);
  bcd_adder bcd_adder_2 (
    .in_1(storage_4_bcd_1_out_28[3]), .in_2(storage_4_bcd_1_out_28[2]), .in_3(storage_4_bcd_1_out_28[1]),
    .in_4(storage_4_bcd_1_out_28[0]), .in_5(storage_4_bcd_1_out_32[3]), .in_6(storage_4_bcd_1_out_32[2]),
    .in_7(storage_4_bcd_1_out_32[1]), .in_8(storage_4_bcd_1_out_32[0]), .in_9(bcd_adder_3_out_11),
    .in_10(1'b1), .out_11(bcd_adder_2_out_11), .out_12(bcd_adder_2_out_15[3]),
    .out_13(bcd_adder_2_out_15[2]), .out_14(bcd_adder_2_out_15[1]), .out_15(bcd_adder_2_out_15[0]));
  not not_2 (not_2_out, in_1);
  sep_Register sep_register_1 (
    .in_3(and_3_out), .in_4(and_4_out), .in_5(1'b1), .in_6(and_2_out), .out_10(sep_register_1_out_10),
    .out_11(sep_register_1_out_11));  // open: in_1, in_2, in_7, out_8, out_9
  bcd_adder bcd_adder_3 (
    .in_1(storage_4_bcd_1_out_24[3]), .in_2(storage_4_bcd_1_out_24[2]), .in_3(storage_4_bcd_1_out_24[1]),
    .in_4(storage_4_bcd_1_out_24[0]), .in_5(storage_4_bcd_1_out_28[3]), .in_6(storage_4_bcd_1_out_28[2]),
    .in_7(storage_4_bcd_1_out_28[1]), .in_8(storage_4_bcd_1_out_28[0]), .in_9(bcd_adder_4_out_11),
    .in_10(1'b1), .out_11(bcd_adder_3_out_11), .out_12(bcd_adder_3_out_15[3]),
    .out_13(bcd_adder_3_out_15[2]), .out_14(bcd_adder_3_out_15[1]), .out_15(bcd_adder_3_out_15[0]));
  category category_1 (
    .A(sep_register_1_out_10), .B(sep_register_1_out_11), .a_2(category_1_a_2), .b_2(category_1_b_2),
    .c(category_1_c), .d(category_1_d), .e(category_1_e), .f(category_1_f), .g(category_1_g));
  _2bit_Decoder u_2bit_decoder_1 (
    .in_1(sep_register_1_out_10), .in_2(sep_register_1_out_11), .in_3(1'b1), .out_4(n2bit_decoder_1_out_4),
    .out_5(n2bit_decoder_1_out_5), .out_6(n2bit_decoder_1_out_6), .out_7(n2bit_decoder_1_out_7));
  Counter Counter_2 (
    .in_1(1'b1), .in_2(1'b1), .in_3(1'b1), .in_4(1'b1), .in_5(1'b1), .in_6(plus_1_out), .in_7(button_1_out),
    .out_8(Counter_2_out_8), .out_9(Counter_2_out_9), .out_10(Counter_2_out_10), .out_11(Counter_2_out_11));
  _2bit_Decoder u_2bit_decoder_2 (
    .in_1(counter_1_out_10), .in_2(counter_1_out_11), .in_3(not_2_out), .out_4(n2bit_decoder_2_out_4),
    .out_5(n2bit_decoder_2_out_5), .out_6(n2bit_decoder_2_out_6), .out_7(n2bit_decoder_2_out_7));
  bcd_adder bcd_adder_4 (
    .in_1(storage_4_bcd_1_out_20[3]), .in_2(storage_4_bcd_1_out_20[2]), .in_3(storage_4_bcd_1_out_20[1]),
    .in_4(storage_4_bcd_1_out_20[0]), .in_5(storage_4_bcd_1_out_24[3]), .in_6(storage_4_bcd_1_out_24[2]),
    .in_7(storage_4_bcd_1_out_24[1]), .in_8(storage_4_bcd_1_out_24[0]), .in_9(1'b0), .in_10(1'b1),
    .out_11(bcd_adder_4_out_11), .out_12(bcd_adder_4_out_15[3]), .out_13(bcd_adder_4_out_15[2]),
    .out_14(bcd_adder_4_out_15[1]), .out_15(bcd_adder_4_out_15[0]));
  _7_Segment_Display u_7_segment_display_1 (
    .g(category_1_g), .f(category_1_f), .a(category_1_a_2), .b(category_1_b_2), .e(category_1_e),
    .d(category_1_d), .c(category_1_c));  // open: dp
  and and_5 (and_5_out, button_4_out, n2bit_decoder_1_out_7);
  and and_6 (and_6_out, button_5_out, n2bit_decoder_1_out_7);
  and and_7 (and_7_out, plus_1_out, n2bit_decoder_2_out_4);
  and and_8 (and_8_out, button_1_out, n2bit_decoder_2_out_4);
  sep_Register sep_register_2 (
    .in_1(Counter_2_out_11), .in_2(Counter_2_out_10), .in_3(Counter_2_out_9), .in_4(Counter_2_out_8),
    .in_5(1'b1), .in_6(and_7_out), .in_7(and_8_out), .out_8(sep_register_2_out_8),
    .out_9(sep_register_2_out_9), .out_10(sep_register_2_out_10), .out_11(sep_register_2_out_11));
  one_cell one_cell_1 (
    .in_1(1'b1), .A(sep_register_2_out_11), .B(sep_register_2_out_10), .C(sep_register_2_out_9),
    .D(sep_register_2_out_8), .out_11(one_cell_1_out_11), .out_12(one_cell_1_out_12),
    .out_13(one_cell_1_out_13), .out_14(one_cell_1_out_14), .out_6(one_cell_1_out_6),
    .out_7(one_cell_1_out_7), .out_8(one_cell_1_out_8), .out_9(one_cell_1_out_9), .out_10(one_cell_1_out_10),
    .out_15(one_cell_1_out_15), .out_16(one_cell_1_out_16));
  one_cell one_cell_2 (
    .in_1(1'b1), .A(storage_4_bcd_2_out_32[3]), .B(storage_4_bcd_2_out_32[2]), .C(storage_4_bcd_2_out_32[1]),
    .D(storage_4_bcd_2_out_32[0]), .out_6(one_cell_2_out_6), .out_7(one_cell_2_out_7),
    .out_8(one_cell_2_out_8), .out_9(one_cell_2_out_9), .out_10(one_cell_2_out_10),
    .out_15(one_cell_2_out_15), .out_16(one_cell_2_out_16));  // open: out_11, out_12, out_13, out_14
  LED led_8 (.in(n2bit_decoder_2_out_4));
  _7_Segment_Display u_7_segment_display_2 (
    .g(one_cell_1_out_16), .f(one_cell_1_out_15), .a(one_cell_1_out_6), .b(one_cell_1_out_7),
    .e(one_cell_1_out_10), .d(one_cell_1_out_9), .c(one_cell_1_out_8));  // open: dp
  Storage_4_bcd storage_4_bcd_1 (
    .in_1(one_cell_7_out_14), .in_2(one_cell_7_out_13), .in_3(one_cell_7_out_12), .in_4(one_cell_7_out_11),
    .in_5(one_cell_5_out_14), .in_6(one_cell_5_out_13), .in_7(one_cell_5_out_12), .in_8(one_cell_5_out_11),
    .in_9(one_cell_3_out_14), .in_10(one_cell_3_out_13), .in_11(one_cell_3_out_12),
    .in_12(one_cell_3_out_11), .in_13(one_cell_1_out_14), .in_14(one_cell_1_out_13),
    .in_15(one_cell_1_out_12), .in_16(one_cell_1_out_11), .in_17(1'b1), .in_18(and_5_out), .in_19(and_6_out),
    .out_20(storage_4_bcd_1_out_20[0]), .out_21(storage_4_bcd_1_out_20[1]),
    .out_22(storage_4_bcd_1_out_20[2]), .out_23(storage_4_bcd_1_out_20[3]),
    .out_24(storage_4_bcd_1_out_24[0]), .out_25(storage_4_bcd_1_out_24[1]),
    .out_26(storage_4_bcd_1_out_24[2]), .out_27(storage_4_bcd_1_out_24[3]),
    .out_28(storage_4_bcd_1_out_28[0]), .out_29(storage_4_bcd_1_out_28[1]),
    .out_30(storage_4_bcd_1_out_28[2]), .out_31(storage_4_bcd_1_out_28[3]),
    .out_32(storage_4_bcd_1_out_32[0]), .out_33(storage_4_bcd_1_out_32[1]),
    .out_34(storage_4_bcd_1_out_32[2]), .out_35(storage_4_bcd_1_out_32[3]));
  _7_Segment_Display u_7_segment_display_3 (
    .g(one_cell_2_out_16), .f(one_cell_2_out_15), .a(one_cell_2_out_6), .b(one_cell_2_out_7),
    .e(one_cell_2_out_10), .d(one_cell_2_out_9), .c(one_cell_2_out_8));  // open: dp
  and and_9 (and_9_out, plus_1_out, n2bit_decoder_2_out_5);
  and and_10 (and_10_out, button_1_out, n2bit_decoder_2_out_5);
  and and_11 (and_11_out, button_4_out, n2bit_decoder_1_out_6);
  and and_12 (and_12_out, button_5_out, n2bit_decoder_1_out_6);
  sep_Register sep_register_3 (
    .in_1(Counter_2_out_11), .in_2(Counter_2_out_10), .in_3(Counter_2_out_9), .in_4(Counter_2_out_8),
    .in_5(1'b1), .in_6(and_9_out), .in_7(and_10_out), .out_8(sep_register_3_out_8),
    .out_9(sep_register_3_out_9), .out_10(sep_register_3_out_10), .out_11(sep_register_3_out_11));
  one_cell one_cell_3 (
    .in_1(1'b1), .A(sep_register_3_out_11), .B(sep_register_3_out_10), .C(sep_register_3_out_9),
    .D(sep_register_3_out_8), .out_11(one_cell_3_out_11), .out_12(one_cell_3_out_12),
    .out_13(one_cell_3_out_13), .out_14(one_cell_3_out_14), .out_6(one_cell_3_out_6),
    .out_7(one_cell_3_out_7), .out_8(one_cell_3_out_8), .out_9(one_cell_3_out_9), .out_10(one_cell_3_out_10),
    .out_15(one_cell_3_out_15), .out_16(one_cell_3_out_16));
  one_cell one_cell_4 (
    .in_1(1'b1), .A(storage_4_bcd_2_out_28[3]), .B(storage_4_bcd_2_out_28[2]), .C(storage_4_bcd_2_out_28[1]),
    .D(storage_4_bcd_2_out_28[0]), .out_6(one_cell_4_out_6), .out_7(one_cell_4_out_7),
    .out_8(one_cell_4_out_8), .out_9(one_cell_4_out_9), .out_10(one_cell_4_out_10),
    .out_15(one_cell_4_out_15), .out_16(one_cell_4_out_16));  // open: out_11, out_12, out_13, out_14
  LED led_9 (.in(n2bit_decoder_2_out_5));
  _7_Segment_Display u_7_segment_display_4 (
    .g(one_cell_3_out_16), .f(one_cell_3_out_15), .a(one_cell_3_out_6), .b(one_cell_3_out_7),
    .e(one_cell_3_out_10), .d(one_cell_3_out_9), .c(one_cell_3_out_8));  // open: dp
  _7_Segment_Display u_7_segment_display_5 (
    .g(one_cell_4_out_16), .f(one_cell_4_out_15), .a(one_cell_4_out_6), .b(one_cell_4_out_7),
    .e(one_cell_4_out_10), .d(one_cell_4_out_9), .c(one_cell_4_out_8));  // open: dp
  and and_13 (and_13_out, plus_1_out, n2bit_decoder_2_out_6);
  and and_14 (and_14_out, button_1_out, n2bit_decoder_2_out_6);
  Cumilative_expense cumilative_expense_1 (
    .in_1(one_cell_7_out_14), .in_2(one_cell_7_out_13), ._0(one_cell_7_out_12), .in_4(one_cell_7_out_11),
    .in_5(one_cell_5_out_14), .in_6(one_cell_5_out_13), .in_7(one_cell_5_out_12), .in_8(one_cell_5_out_11),
    .in_9(one_cell_3_out_14), .in_10(one_cell_3_out_13), .in_11(one_cell_3_out_12),
    .in_12(one_cell_3_out_11), .in_13(one_cell_1_out_14), .in_14(one_cell_1_out_13),
    .in_15(one_cell_1_out_12), .in_16(one_cell_1_out_11), .in_17(1'b1), .in_18(and_11_out),
    .in_19(and_12_out), .out_20(cumilative_expense_1_out_20[0]), .out_21(cumilative_expense_1_out_20[1]),
    .out_22(cumilative_expense_1_out_20[2]), .out_23(cumilative_expense_1_out_20[3]),
    .out_24(cumilative_expense_1_out_24[0]), .out_25(cumilative_expense_1_out_24[1]),
    .out_26(cumilative_expense_1_out_24[2]), .out_27(cumilative_expense_1_out_24[3]),
    .out_28(cumilative_expense_1_out_28[0]), .out_29(cumilative_expense_1_out_28[1]),
    .out_30(cumilative_expense_1_out_28[2]), .out_31(cumilative_expense_1_out_28[3]),
    .out_32(cumilative_expense_1_out_32[0]), .out_33(cumilative_expense_1_out_32[1]),
    .out_34(cumilative_expense_1_out_32[2]), .out_35(cumilative_expense_1_out_32[3]));  // open: out_36
  sep_Register sep_register_4 (
    .in_1(Counter_2_out_11), .in_2(Counter_2_out_10), .in_3(Counter_2_out_9), .in_4(Counter_2_out_8),
    .in_5(1'b1), .in_6(and_13_out), .in_7(and_14_out), .out_8(sep_register_4_out_8),
    .out_9(sep_register_4_out_9), .out_10(sep_register_4_out_10), .out_11(sep_register_4_out_11));
  one_cell one_cell_5 (
    .in_1(1'b1), .A(sep_register_4_out_11), .B(sep_register_4_out_10), .C(sep_register_4_out_9),
    .D(sep_register_4_out_8), .out_11(one_cell_5_out_11), .out_12(one_cell_5_out_12),
    .out_13(one_cell_5_out_13), .out_14(one_cell_5_out_14), .out_6(one_cell_5_out_6),
    .out_7(one_cell_5_out_7), .out_8(one_cell_5_out_8), .out_9(one_cell_5_out_9), .out_10(one_cell_5_out_10),
    .out_15(one_cell_5_out_15), .out_16(one_cell_5_out_16));
  one_cell one_cell_6 (
    .in_1(1'b1), .A(storage_4_bcd_2_out_24[3]), .B(storage_4_bcd_2_out_24[2]), .C(storage_4_bcd_2_out_24[1]),
    .D(storage_4_bcd_2_out_24[0]), .out_6(one_cell_6_out_6), .out_7(one_cell_6_out_7),
    .out_8(one_cell_6_out_8), .out_9(one_cell_6_out_9), .out_10(one_cell_6_out_10),
    .out_15(one_cell_6_out_15), .out_16(one_cell_6_out_16));  // open: out_11, out_12, out_13, out_14
  LED led_10 (.in(n2bit_decoder_2_out_6));
  and and_15 (and_15_out, button_4_out, n2bit_decoder_1_out_5);
  and and_16 (and_16_out, button_5_out, n2bit_decoder_1_out_5);
  and and_17 (and_17_out, plus_1_out, n2bit_decoder_2_out_7);
  _7_Segment_Display u_7_segment_display_6 (
    .g(one_cell_5_out_16), .f(one_cell_5_out_15), .a(one_cell_5_out_6), .b(one_cell_5_out_7),
    .e(one_cell_5_out_10), .d(one_cell_5_out_9), .c(one_cell_5_out_8));  // open: dp
  _7_Segment_Display u_7_segment_display_7 (
    .g(one_cell_6_out_16), .f(one_cell_6_out_15), .a(one_cell_6_out_6), .b(one_cell_6_out_7),
    .e(one_cell_6_out_10), .d(one_cell_6_out_9), .c(one_cell_6_out_8));  // open: dp
  and and_18 (and_18_out, button_1_out, n2bit_decoder_2_out_7);
  sep_Register sep_register_5 (
    .in_1(Counter_2_out_11), .in_2(Counter_2_out_10), .in_3(Counter_2_out_9), .in_4(Counter_2_out_8),
    .in_5(1'b1), .in_6(and_17_out), .in_7(and_18_out), .out_8(sep_register_5_out_8),
    .out_9(sep_register_5_out_9), .out_10(sep_register_5_out_10), .out_11(sep_register_5_out_11));
  one_cell one_cell_7 (
    .in_1(1'b1), .A(sep_register_5_out_11), .B(sep_register_5_out_10), .C(sep_register_5_out_9),
    .D(sep_register_5_out_8), .out_11(one_cell_7_out_11), .out_12(one_cell_7_out_12),
    .out_13(one_cell_7_out_13), .out_14(one_cell_7_out_14), .out_6(one_cell_7_out_6),
    .out_7(one_cell_7_out_7), .out_8(one_cell_7_out_8), .out_9(one_cell_7_out_9), .out_10(one_cell_7_out_10),
    .out_15(one_cell_7_out_15), .out_16(one_cell_7_out_16));
  Cumilative_expense cumilative_expense_2 (
    .in_1(one_cell_7_out_14), .in_2(one_cell_7_out_13), ._0(one_cell_7_out_12), .in_4(one_cell_7_out_11),
    .in_5(one_cell_5_out_14), .in_6(one_cell_5_out_13), .in_7(one_cell_5_out_12), .in_8(one_cell_5_out_11),
    .in_9(one_cell_3_out_14), .in_10(one_cell_3_out_13), .in_11(one_cell_3_out_12),
    .in_12(one_cell_3_out_11), .in_13(one_cell_1_out_14), .in_14(one_cell_1_out_13),
    .in_15(one_cell_1_out_12), .in_16(one_cell_1_out_11), .in_17(1'b1), .in_18(and_15_out),
    .in_19(and_16_out), .out_20(cumilative_expense_2_out_20[0]), .out_21(cumilative_expense_2_out_20[1]),
    .out_22(cumilative_expense_2_out_20[2]), .out_23(cumilative_expense_2_out_20[3]),
    .out_24(cumilative_expense_2_out_20[4]), .out_25(cumilative_expense_2_out_20[5]),
    .out_26(cumilative_expense_2_out_20[6]), .out_27(cumilative_expense_2_out_20[7]),
    .out_28(cumilative_expense_2_out_20[8]), .out_29(cumilative_expense_2_out_20[9]),
    .out_30(cumilative_expense_2_out_20[10]), .out_31(cumilative_expense_2_out_20[11]),
    .out_32(cumilative_expense_2_out_20[12]), .out_33(cumilative_expense_2_out_20[13]),
    .out_34(cumilative_expense_2_out_20[14]), .out_35(cumilative_expense_2_out_20[15]));  // open: out_36
  one_cell one_cell_8 (
    .in_1(1'b1), .A(storage_4_bcd_2_out_20[3]), .B(storage_4_bcd_2_out_20[2]), .C(storage_4_bcd_2_out_20[1]),
    .D(storage_4_bcd_2_out_20[0]), .out_6(one_cell_8_out_6), .out_7(one_cell_8_out_7),
    .out_8(one_cell_8_out_8), .out_9(one_cell_8_out_9), .out_10(one_cell_8_out_10),
    .out_15(one_cell_8_out_15), .out_16(one_cell_8_out_16));  // open: out_11, out_12, out_13, out_14
  LED led_11 (.in(n2bit_decoder_2_out_7));
  _7_Segment_Display u_7_segment_display_8 (
    .g(one_cell_7_out_16), .f(one_cell_7_out_15), .a(one_cell_7_out_6), .b(one_cell_7_out_7),
    .e(one_cell_7_out_10), .d(one_cell_7_out_9), .c(one_cell_7_out_8));  // open: dp
  or or_1 (or_1_out, and_15_out, and_11_out);
  and and_19 (and_19_out, button_5_out, n2bit_decoder_1_out_4);
  _7_Segment_Display u_7_segment_display_9 (
    .g(one_cell_8_out_16), .f(one_cell_8_out_15), .a(one_cell_8_out_6), .b(one_cell_8_out_7),
    .e(one_cell_8_out_10), .d(one_cell_8_out_9), .c(one_cell_8_out_8));  // open: dp
  not not_3 (not_3_out, or_1_out);
  bcd_adder bcd_adder_5 (
    .in_1(cumilative_expense_2_out_20[15]), .in_2(cumilative_expense_2_out_20[14]),
    .in_3(cumilative_expense_2_out_20[13]), .in_4(cumilative_expense_2_out_20[12]),
    .in_5(cumilative_expense_1_out_32[3]), .in_6(cumilative_expense_1_out_32[2]),
    .in_7(cumilative_expense_1_out_32[1]), .in_8(cumilative_expense_1_out_32[0]), .in_9(bcd_adder_6_out_11),
    .in_10(1'b0), .out_12(bcd_adder_5_out_12), .out_13(bcd_adder_5_out_13), .out_14(bcd_adder_5_out_14),
    .out_15(bcd_adder_5_out_15));  // open: out_11
  Storage_4_bcd storage_4_bcd_2 (
    .in_1(bcd_adder_8_out_15), .in_2(bcd_adder_8_out_14), .in_3(bcd_adder_8_out_13),
    .in_4(bcd_adder_8_out_12), .in_5(bcd_adder_7_out_15), .in_6(bcd_adder_7_out_14),
    .in_7(bcd_adder_7_out_13), .in_8(bcd_adder_7_out_12), .in_9(bcd_adder_6_out_15),
    .in_10(bcd_adder_6_out_14), .in_11(bcd_adder_6_out_13), .in_12(bcd_adder_6_out_12),
    .in_13(bcd_adder_5_out_15), .in_14(bcd_adder_5_out_14), .in_15(bcd_adder_5_out_13),
    .in_16(bcd_adder_5_out_12), .in_17(1'b1), .in_18(not_3_out), .in_19(and_19_out),
    .out_20(storage_4_bcd_2_out_20[0]), .out_21(storage_4_bcd_2_out_20[1]),
    .out_22(storage_4_bcd_2_out_20[2]), .out_23(storage_4_bcd_2_out_20[3]),
    .out_24(storage_4_bcd_2_out_24[0]), .out_25(storage_4_bcd_2_out_24[1]),
    .out_26(storage_4_bcd_2_out_24[2]), .out_27(storage_4_bcd_2_out_24[3]),
    .out_28(storage_4_bcd_2_out_28[0]), .out_29(storage_4_bcd_2_out_28[1]),
    .out_30(storage_4_bcd_2_out_28[2]), .out_31(storage_4_bcd_2_out_28[3]),
    .out_32(storage_4_bcd_2_out_32[0]), .out_33(storage_4_bcd_2_out_32[1]),
    .out_34(storage_4_bcd_2_out_32[2]), .out_35(storage_4_bcd_2_out_32[3]));
  bcd_adder bcd_adder_6 (
    .in_1(cumilative_expense_2_out_20[11]), .in_2(cumilative_expense_2_out_20[10]),
    .in_3(cumilative_expense_2_out_20[9]), .in_4(cumilative_expense_2_out_20[8]),
    .in_5(cumilative_expense_1_out_28[3]), .in_6(cumilative_expense_1_out_28[2]),
    .in_7(cumilative_expense_1_out_28[1]), .in_8(cumilative_expense_1_out_28[0]), .in_9(bcd_adder_7_out_11),
    .in_10(1'b0), .out_11(bcd_adder_6_out_11), .out_12(bcd_adder_6_out_12), .out_13(bcd_adder_6_out_13),
    .out_14(bcd_adder_6_out_14), .out_15(bcd_adder_6_out_15));
  bcd_adder bcd_adder_7 (
    .in_1(cumilative_expense_2_out_20[7]), .in_2(cumilative_expense_2_out_20[6]),
    .in_3(cumilative_expense_2_out_20[5]), .in_4(cumilative_expense_2_out_20[4]),
    .in_5(cumilative_expense_1_out_24[3]), .in_6(cumilative_expense_1_out_24[2]),
    .in_7(cumilative_expense_1_out_24[1]), .in_8(cumilative_expense_1_out_24[0]), .in_9(bcd_adder_8_out_11),
    .in_10(1'b0), .out_11(bcd_adder_7_out_11), .out_12(bcd_adder_7_out_12), .out_13(bcd_adder_7_out_13),
    .out_14(bcd_adder_7_out_14), .out_15(bcd_adder_7_out_15));
  bcd_adder bcd_adder_8 (
    .in_1(cumilative_expense_2_out_20[3]), .in_2(cumilative_expense_2_out_20[2]),
    .in_3(cumilative_expense_2_out_20[1]), .in_4(cumilative_expense_2_out_20[0]),
    .in_5(cumilative_expense_1_out_20[3]), .in_6(cumilative_expense_1_out_20[2]),
    .in_7(cumilative_expense_1_out_20[1]), .in_8(cumilative_expense_1_out_20[0]), .in_9(1'b0), .in_10(1'b0),
    .out_11(bcd_adder_8_out_11), .out_12(bcd_adder_8_out_12), .out_13(bcd_adder_8_out_13),
    .out_14(bcd_adder_8_out_14), .out_15(bcd_adder_8_out_15));

  // Notes on the sheet:
  //   Category Display
  //   D -> Budget
  //   B -> Bills
  //   C -> Cumulative
  //   A -> Additional Expense
  //   Cumulative =Additonal Expense + Bills
  //   Change Category/Input digit
  //   Return to Budget
  //   Yellow LED
  //   Green LED
  //   Increment by 1
  //   Reset to 0
  //   0 -> Input Part
  //   1 -> Category Part
  //   Save Value
  //   Reset Value
  //   Red LED
  //   Red- Expense>100% of Budget
  //   Yellow- Expense>90% of Budget
  //   Green- Expense<90% of Budget
  //   BCD adder subtractors
  //   Switch 
  //   counter
  //   register 
  //   BCD comparator
  //   Counter. Blue:To increase the value by one.Red: to reset it to zero
  //   2 bit encoder
  //   Category display
  //   D-BUDGET
  //   eX_Calci
  //   INPUT PART
  //   7 segment display
  //   Registers to store the input values
  //   7 segment display
  //   A-Additional Expense
  //   -know your expenses like never before
  //   The Cumulative
  //   7 segment display
  //   B- Bills
  //   7 segment display
  //   C-Cumilative
  //   accumulators
  //   16 bit storage
endmodule

module bcd_7seg (
  input  A,
  input  B,
  input  C,
  input  D,
  output out_5,
  output out_6,
  output out_7,
  output out_8,
  output out_9,
  output out_10,
  output out_11
);

  wire and_1_out, and_2_out, and_3_out, and_4_out, and_5_out, and_6_out, and_7_out, and_8_out, and_9_out,
       not_1_out, not_2_out, not_3_out, or_1_out, or_2_out, or_3_out, or_7_out, or_9_out, or_10_out,
       or_11_out, or_13_out;

  not not_1 (not_1_out, B);
  not not_2 (not_2_out, C);
  not not_3 (not_3_out, D);
  and and_1 (and_1_out, B, D);
  and and_2 (and_2_out, not_1_out, C);
  and and_3 (and_3_out, C, D);
  and and_4 (and_4_out, not_1_out, not_3_out);
  and and_5 (and_5_out, not_2_out, B);
  and and_6 (and_6_out, not_2_out, B, D);
  and and_7 (and_7_out, C, not_3_out);
  and and_8 (and_8_out, not_3_out, B);
  and and_9 (and_9_out, not_3_out, not_2_out);
  or or_1 (or_1_out, A, and_2_out);
  or or_2 (or_2_out, and_5_out, and_8_out);
  or or_3 (or_3_out, A, and_9_out);
  or or_4 (out_9, and_4_out, and_7_out);
  or or_5 (out_10, or_3_out, or_2_out);
  or or_6 (out_11, or_1_out, or_2_out);
  or or_7 (or_7_out, C, and_4_out);
  or or_8 (out_6, not_1_out, or_9_out);
  or or_9 (or_9_out, and_9_out, and_3_out);
  or or_10 (or_10_out, B, not_2_out);
  or or_11 (or_11_out, and_6_out, or_1_out);
  or or_12 (out_5, A, or_13_out);
  or or_13 (or_13_out, and_1_out, or_7_out);
  or or_14 (out_7, D, or_10_out);
  or or_15 (out_8, or_11_out, out_9);
endmodule

module one_cell (
  input  in_1,
  input  A,
  input  B,
  input  C,
  input  D,
  output out_6,
  output out_7,
  output out_8,
  output out_9,
  output out_10,
  output out_11,
  output out_12,
  output out_13,
  output out_14,
  output out_15,
  output out_16
);

  and and_1 (out_11, A, in_1);
  and and_2 (out_12, B, in_1);
  and and_3 (out_13, C, in_1);
  and and_4 (out_14, D, in_1);
  bcd_7seg bcd_7seg_1 (
    .A(out_11), .B(out_12), .C(out_13), .D(out_14), .out_5(out_6), .out_6(out_7), .out_7(out_8),
    .out_8(out_9), .out_9(out_10), .out_10(out_15), .out_11(out_16));
endmodule

module category (
  input  A,
  input  B,
  output a_2,
  output b_2,
  output c,
  output d,
  output e,
  output f,
  output g
);

  wire not_1_out;

  not not_1 (not_1_out, B);
  nand nand_1 (b_2, A, B);
  nand nand_2 (c, A, B);
  or or_1 (d, not_1_out, A);
  xor xor_1 (g, B, A);

  assign a_2 = 1'b1;
  assign e = 1'b1;
  assign f = 1'b1;
endmodule

// 4bit flip flop
module sep_Register (
  input  in_1,
  input  in_2,
  input  in_3,
  input  in_4,
  input  in_5,
  input  in_6,
  input  in_7,
  output out_8,
  output out_9,
  output out_10,
  output out_11
);

  D_Flip_Flop d_ff_1 (.clk(in_6), .D(in_1), .Q(out_8), .en(in_5), .reset(in_7));  // open: Qn, preset
  D_Flip_Flop d_ff_2 (.clk(in_6), .D(in_2), .Q(out_9), .en(in_5), .reset(in_7));  // open: Qn, preset
  D_Flip_Flop d_ff_3 (.clk(in_6), .D(in_3), .Q(out_10), .en(in_5), .reset(in_7));  // open: Qn, preset
  D_Flip_Flop d_ff_4 (.clk(in_6), .D(in_4), .Q(out_11), .en(in_5), .reset(in_7));  // open: Qn, preset
endmodule

module Reconnect22 (
  input  a,
  input  b,
  input  c,
  input  d,
  input  e,
  output a2,
  output b2,
  output c2,
  output d2
);

  wire and_1_out, and_2_out, and_3_out, and_4_out, and_5_out, and_6_out, and_7_out, and_8_out, and_9_out,
       and_10_out, and_11_out, and_12_out, and_13_out, not_1_out, not_2_out, not_3_out, or_2_out;

  and and_1 (and_1_out, a, e);
  and and_2 (and_2_out, b, e);
  and and_3 (and_3_out, c, e);
  and and_4 (and_4_out, d, e);
  not not_1 (not_1_out, and_2_out);
  not not_2 (not_2_out, and_1_out);
  not not_3 (not_3_out, and_3_out);
  not not_4 (d2, and_4_out);
  and and_5 (and_5_out, and_1_out, d2);
  and and_6 (and_6_out, and_3_out, and_4_out);
  and and_7 (and_7_out, and_2_out, d2);
  and and_8 (and_8_out, not_2_out, not_3_out);
  and and_9 (and_9_out, and_2_out, and_6_out);
  and and_10 (and_10_out, not_1_out, and_6_out);
  and and_11 (and_11_out, and_2_out, not_3_out);
  and and_12 (and_12_out, and_8_out, and_4_out);
  and and_13 (and_13_out, and_3_out, d2);
  or or_1 (a2, and_9_out, and_5_out);
  or or_2 (or_2_out, and_10_out, and_11_out);
  or or_3 (c2, and_12_out, and_13_out);
  or or_4 (b2, or_2_out, and_7_out);
endmodule

module Storage_4_bcd (
  input  in_1,
  input  in_2,
  input  in_3,
  input  in_4,
  input  in_5,
  input  in_6,
  input  in_7,
  input  in_8,
  input  in_9,
  input  in_10,
  input  in_11,
  input  in_12,
  input  in_13,
  input  in_14,
  input  in_15,
  input  in_16,
  input  in_17,
  input  in_18,
  input  in_19,
  output out_20,
  output out_21,
  output out_22,
  output out_23,
  output out_24,
  output out_25,
  output out_26,
  output out_27,
  output out_28,
  output out_29,
  output out_30,
  output out_31,
  output out_32,
  output out_33,
  output out_34,
  output out_35
);

  D_Flip_Flop d_ff_1 (.clk(in_18), .D(in_1), .Q(out_20), .en(in_17), .reset(in_19));  // open: Qn, preset
  D_Flip_Flop d_ff_2 (.clk(in_18), .D(in_2), .Q(out_21), .en(in_17), .reset(in_19));  // open: Qn, preset
  D_Flip_Flop d_ff_3 (.clk(in_18), .D(in_3), .Q(out_22), .en(in_17), .reset(in_19));  // open: Qn, preset
  D_Flip_Flop d_ff_4 (.clk(in_18), .D(in_4), .Q(out_23), .en(in_17), .reset(in_19));  // open: Qn, preset
  D_Flip_Flop d_ff_5 (.clk(in_18), .D(in_5), .Q(out_24), .en(in_17), .reset(in_19));  // open: Qn, preset
  D_Flip_Flop d_ff_6 (.clk(in_18), .D(in_6), .Q(out_25), .en(in_17), .reset(in_19));  // open: Qn, preset
  D_Flip_Flop d_ff_7 (.clk(in_18), .D(in_7), .Q(out_26), .en(in_17), .reset(in_19));  // open: Qn, preset
  D_Flip_Flop d_ff_8 (.clk(in_18), .D(in_8), .Q(out_27), .en(in_17), .reset(in_19));  // open: Qn, preset
  D_Flip_Flop d_ff_9 (.clk(in_18), .D(in_9), .Q(out_28), .en(in_17), .reset(in_19));  // open: Qn, preset
  D_Flip_Flop d_ff_10 (.clk(in_18), .D(in_10), .Q(out_29), .en(in_17), .reset(in_19));  // open: Qn, preset
  D_Flip_Flop d_ff_11 (.clk(in_18), .D(in_11), .Q(out_30), .en(in_17), .reset(in_19));  // open: Qn, preset
  D_Flip_Flop d_ff_12 (.clk(in_18), .D(in_12), .Q(out_31), .en(in_17), .reset(in_19));  // open: Qn, preset
  D_Flip_Flop d_ff_13 (.clk(in_18), .D(in_13), .Q(out_32), .en(in_17), .reset(in_19));  // open: Qn, preset
  D_Flip_Flop d_ff_14 (.clk(in_18), .D(in_14), .Q(out_33), .en(in_17), .reset(in_19));  // open: Qn, preset
  D_Flip_Flop d_ff_15 (.clk(in_18), .D(in_15), .Q(out_34), .en(in_17), .reset(in_19));  // open: Qn, preset
  D_Flip_Flop d_ff_16 (.clk(in_18), .D(in_16), .Q(out_35), .en(in_17), .reset(in_19));  // open: Qn, preset
endmodule

module _2bit_Decoder (
  input  in_1,
  input  in_2,
  input  in_3,
  output out_4,
  output out_5,
  output out_6,
  output out_7
);

  wire and_1_out, and_2_out, not_1_out, not_2_out;

  and and_1 (and_1_out, in_1, in_3);
  and and_2 (and_2_out, in_2, in_3);
  not not_1 (not_1_out, and_1_out);
  not not_2 (not_2_out, and_2_out);
  nor nor_1 (out_7, and_1_out, and_2_out);
  and and_3 (out_6, not_1_out, and_2_out);
  and and_4 (out_5, and_1_out, not_2_out);
  and and_5 (out_4, and_1_out, and_2_out);
endmodule

module Counter (
  input  in_1,
  input  in_2,
  input  in_3,
  input  in_4,
  input  in_5,
  input  in_6,
  input  in_7,
  output out_8,
  output out_9,
  output out_10,
  output out_11
);

  wire and_1_out, and_2_out, and_3_out, and_4_out, reconnect22_1_a2, reconnect22_1_b2, reconnect22_1_c2,
       reconnect22_1_d2;

  Reconnect22 reconnect22_1 (
    .a(out_8), .b(out_9), .c(out_10), .d(out_11), .e(in_5), .a2(reconnect22_1_a2), .b2(reconnect22_1_b2),
    .c2(reconnect22_1_c2), .d2(reconnect22_1_d2));
  and and_1 (and_1_out, in_1, reconnect22_1_a2);
  and and_2 (and_2_out, in_2, reconnect22_1_b2);
  and and_3 (and_3_out, in_3, reconnect22_1_c2);
  and and_4 (and_4_out, in_4, reconnect22_1_d2);
  sep_Register sep_register_1 (
    .in_1(and_1_out), .in_2(and_2_out), .in_3(and_3_out), .in_4(and_4_out), .in_5(in_5), .in_6(in_6),
    .in_7(in_7), .out_8(out_8), .out_9(out_9), .out_10(out_10), .out_11(out_11));
endmodule

module bcd_adder (
  input  in_1,
  input  in_2,
  input  in_3,
  input  in_4,
  input  in_5,
  input  in_6,
  input  in_7,
  input  in_8,
  input  in_9,
  input  in_10,
  output out_11,
  output out_12,
  output out_13,
  output out_14,
  output out_15
);

  wire adder_1_cout, adder_2_cout, and_1_out, and_2_out, and_3_out, and_6_out, and_7_out, and_8_out,
       not_1_out, not_2_out, not_3_out, not_4_out, not_5_out, or_1_out, xor_5_out, xor_6_out, xor_7_out,
       xor_8_out;
  wire [2:0] and_5_out;
  wire [3:0] adder_1_out, adder_2_out, xor_4_out;

  xor xor_1 (xor_4_out[3], in_5, in_10);
  xor xor_2 (xor_4_out[2], in_6, in_10);
  xor xor_3 (xor_4_out[1], in_7, in_10);
  xor xor_4 (xor_4_out[0], in_8, in_10);
  and and_1 (and_1_out, in_9, not_1_out);
  not not_1 (not_1_out, in_10);
  not not_2 (not_2_out, in_9);
  Adder #(.width(4)) adder_1 (
    .a({in_1, in_2, in_3, in_4}), .b(xor_4_out), .out(adder_1_out), .cin(and_1_out), .cout(adder_1_cout));
  not not_3 (not_3_out, in_10);
  not not_4 (not_4_out, adder_1_cout);
  and and_2 (and_2_out, adder_1_out[1], adder_1_out[3]);
  and and_3 (and_3_out, adder_1_out[2], adder_1_out[3]);
  or or_1 (or_1_out, adder_1_cout, and_2_out, and_3_out);
  and and_4 (and_5_out[2], or_1_out, not_3_out);
  and and_5 (and_5_out[0], in_10, not_2_out, adder_1_cout);
  and and_6 (and_6_out, not_4_out, in_10);
  Adder #(.width(4)) adder_2 (
    .a(adder_1_out), .b({1'b0, {2{and_5_out[2]}}, and_5_out[0]}), .out(adder_2_out), .cin(1'b0),
    .cout(adder_2_cout));
  not not_5 (not_5_out, in_10);
  xor xor_5 (xor_5_out, adder_2_out[3], and_6_out);
  xor xor_6 (xor_6_out, adder_2_out[2], and_6_out);
  xor xor_7 (xor_7_out, adder_2_out[1], and_6_out);
  xor xor_8 (xor_8_out, adder_2_out[0], and_6_out);
  and and_7 (and_7_out, not_5_out, and_5_out[2]);
  and and_8 (and_8_out, in_10, and_6_out);
  or or_2 (out_11, and_7_out, and_8_out);
  _10_k_ckt2 u_10_k_ckt2_1 (
    .a(xor_5_out), .b(xor_6_out), .c(xor_7_out), .d(xor_8_out), .in_5(and_6_out), .q(out_12), .w(out_13),
    .e(out_14), .r(out_15));
endmodule

module _10_k_ckt2 (
  input  a,
  input  b,
  input  c,
  input  d,
  input  in_5,
  output q,
  output w,
  output e,
  output r
);

  wire and_1_out, and_2_out, and_3_out, and_4_out, and_5_out, and_6_out, and_7_out, and_8_out, and_9_out,
       and_10_out, and_11_out, and_12_out, and_13_out, and_14_out, and_15_out, nor_1_out, not_1_out,
       not_2_out, not_3_out, not_4_out, or_1_out, or_2_out, or_3_out, or_4_out, xor_1_out;

  not not_1 (not_1_out, b);
  not not_2 (not_2_out, c);
  not not_3 (not_3_out, d);
  nor nor_1 (nor_1_out, a, b);
  xor xor_1 (xor_1_out, c, d);
  and and_1 (and_1_out, c, d);
  and and_2 (and_2_out, b, not_2_out);
  and and_3 (and_3_out, nor_1_out, xor_1_out);
  and and_4 (and_4_out, not_1_out, and_1_out);
  and and_5 (and_5_out, and_2_out, not_3_out);
  or or_1 (or_1_out, and_4_out, and_2_out);
  and and_6 (and_6_out, b, not_3_out);
  or or_2 (or_2_out, and_1_out, and_5_out);
  and and_7 (and_7_out, a, not_3_out);
  not not_4 (not_4_out, in_5);
  and and_8 (and_8_out, and_3_out, in_5);
  and and_9 (and_9_out, in_5, or_3_out);
  or or_3 (or_3_out, or_1_out, and_6_out);
  or or_4 (or_4_out, or_2_out, and_7_out);
  and and_10 (and_10_out, or_4_out, in_5);
  and and_11 (and_11_out, in_5, d);
  and and_12 (and_12_out, a, not_4_out);
  and and_13 (and_13_out, b, not_4_out);
  and and_14 (and_14_out, c, not_4_out);
  and and_15 (and_15_out, d, not_4_out);
  or or_5 (q, and_12_out, and_8_out);
  or or_6 (w, and_13_out, and_9_out);
  or or_7 (e, and_14_out, and_10_out);
  or or_8 (r, and_15_out, and_11_out);
endmodule

module Cumilative_expense (
  input  in_1,
  input  in_2,
  input  _0,
  input  in_4,
  input  in_5,
  input  in_6,
  input  in_7,
  input  in_8,
  input  in_9,
  input  in_10,
  input  in_11,
  input  in_12,
  input  in_13,
  input  in_14,
  input  in_15,
  input  in_16,
  input  in_17,
  input  in_18,
  input  in_19,
  output out_20,
  output out_21,
  output out_22,
  output out_23,
  output out_24,
  output out_25,
  output out_26,
  output out_27,
  output out_28,
  output out_29,
  output out_30,
  output out_31,
  output out_32,
  output out_33,
  output out_34,
  output out_35,
  output out_36
);

  wire bcd_adder_1_out_11, bcd_adder_1_out_12, bcd_adder_1_out_13, bcd_adder_1_out_14, bcd_adder_1_out_15,
       bcd_adder_2_out_11, bcd_adder_2_out_12, bcd_adder_2_out_13, bcd_adder_2_out_14, bcd_adder_2_out_15,
       bcd_adder_3_out_11, bcd_adder_3_out_12, bcd_adder_3_out_13, bcd_adder_3_out_14, bcd_adder_3_out_15,
       bcd_adder_4_out_12, bcd_adder_4_out_13, bcd_adder_4_out_14, bcd_adder_4_out_15;

  bcd_adder bcd_adder_1 (
    .in_1(out_23), .in_2(out_22), .in_3(out_21), .in_4(out_20), .in_5(in_4), .in_6(_0), .in_7(in_2),
    .in_8(in_1), .in_9(1'b0), .in_10(1'b0), .out_11(bcd_adder_1_out_11), .out_12(bcd_adder_1_out_12),
    .out_13(bcd_adder_1_out_13), .out_14(bcd_adder_1_out_14), .out_15(bcd_adder_1_out_15));
  bcd_adder bcd_adder_2 (
    .in_1(out_27), .in_2(out_26), .in_3(out_25), .in_4(out_24), .in_5(in_8), .in_6(in_7), .in_7(in_6),
    .in_8(in_5), .in_9(bcd_adder_1_out_11), .in_10(1'b0), .out_11(bcd_adder_2_out_11),
    .out_12(bcd_adder_2_out_12), .out_13(bcd_adder_2_out_13), .out_14(bcd_adder_2_out_14),
    .out_15(bcd_adder_2_out_15));
  bcd_adder bcd_adder_3 (
    .in_1(out_31), .in_2(out_30), .in_3(out_29), .in_4(out_28), .in_5(in_12), .in_6(in_11), .in_7(in_10),
    .in_8(in_9), .in_9(bcd_adder_2_out_11), .in_10(1'b0), .out_11(bcd_adder_3_out_11),
    .out_12(bcd_adder_3_out_12), .out_13(bcd_adder_3_out_13), .out_14(bcd_adder_3_out_14),
    .out_15(bcd_adder_3_out_15));
  bcd_adder bcd_adder_4 (
    .in_1(out_35), .in_2(out_34), .in_3(out_33), .in_4(out_32), .in_5(in_16), .in_6(in_15), .in_7(in_14),
    .in_8(in_13), .in_9(bcd_adder_3_out_11), .in_10(1'b0), .out_11(out_36), .out_12(bcd_adder_4_out_12),
    .out_13(bcd_adder_4_out_13), .out_14(bcd_adder_4_out_14), .out_15(bcd_adder_4_out_15));
  Storage_4_bcd storage_4_bcd_1 (
    .in_1(bcd_adder_1_out_15), .in_2(bcd_adder_1_out_14), .in_3(bcd_adder_1_out_13),
    .in_4(bcd_adder_1_out_12), .in_5(bcd_adder_2_out_15), .in_6(bcd_adder_2_out_14),
    .in_7(bcd_adder_2_out_13), .in_8(bcd_adder_2_out_12), .in_9(bcd_adder_3_out_15),
    .in_10(bcd_adder_3_out_14), .in_11(bcd_adder_3_out_13), .in_12(bcd_adder_3_out_12),
    .in_13(bcd_adder_4_out_15), .in_14(bcd_adder_4_out_14), .in_15(bcd_adder_4_out_13),
    .in_16(bcd_adder_4_out_12), .in_17(in_17), .in_18(in_18), .in_19(in_19), .out_20(out_20),
    .out_21(out_21), .out_22(out_22), .out_23(out_23), .out_24(out_24), .out_25(out_25), .out_26(out_26),
    .out_27(out_27), .out_28(out_28), .out_29(out_29), .out_30(out_30), .out_31(out_31), .out_32(out_32),
    .out_33(out_33), .out_34(out_34), .out_35(out_35));
endmodule

module BCD_compare (
  input  [3:0] in_1,
  input  [3:0] in_2,
  input  [3:0] in_3,
  input  [3:0] in_4,
  input  [3:0] in_5,
  input  [3:0] in_6,
  input  [3:0] in_7,
  input  [3:0] in_8,
  output out_9
);

  wire and_1_out, and_2_out, and_3_out, comparator_1_eq, comparator_1_lt, comparator_2_eq, comparator_2_lt,
       comparator_3_eq, comparator_3_lt, comparator_4_lt;

  LED led_1 (.in(out_9));
  or or_1 (out_9, comparator_1_lt, and_1_out, and_2_out, and_3_out);
  and and_1 (and_1_out, comparator_1_eq, comparator_2_lt);
  Comparator #(.width(4), .mode("unsigned")) comparator_1 (
    .a(in_1), .b(in_2), .eq(comparator_1_eq), .lt(comparator_1_lt));  // open: gt
  and and_2 (and_2_out, comparator_2_eq, comparator_3_lt, comparator_1_eq);
  Comparator #(.width(4), .mode("unsigned")) comparator_2 (
    .a(in_3), .b(in_4), .eq(comparator_2_eq), .lt(comparator_2_lt));  // open: gt
  Comparator #(.width(4), .mode("unsigned")) comparator_3 (
    .a(in_5), .b(in_6), .eq(comparator_3_eq), .lt(comparator_3_lt));  // open: gt
  and and_3 (and_3_out, comparator_2_eq, comparator_3_eq, comparator_1_eq, comparator_4_lt);
  Comparator #(.width(4), .mode("unsigned")) comparator_4 (.a(in_7), .b(in_8), .lt(comparator_4_lt));  // open: gt, eq
endmodule
